# Fritzing sketch tb_projekt_rfboard_v1_3 (saved by Fritzing 0.9.2b)
circuit board: 6.9215cm x 5.33756cm
breadboards: 2

parts:
  S2 = Pushbutton [package="[THT]"]
  XTAL1 = Crystal [frequency="16 Mhz" package=THT]
  R1 = Resistor [tolerance=±5% resistance=10k package=THT]
  C8 = Ceramic Capacitor [capacitance=100nF package="100 mil [THT, multilayer]"]
  C9 = Ceramic Capacitor [capacitance=100nF package="100 mil [THT, multilayer]"]
  C10 = Ceramic Capacitor [capacitance=100nF package="100 mil [THT, multilayer]"]
  J6 = male pin header, 6 pins [form="♂ (male)"]
  Power = Power plug
  D1 = Rectifier Diode [part_number=1N4001 package="300 mil [THT]"]
  C11 = Electrolytic Capacitor [capacitance=10µF package="100 mil [THT, electrolytic]"]
  C12 = Ceramic Capacitor [capacitance=100nF package="100 mil [THT, multilayer]"]
  C13 = Ceramic Capacitor [capacitance=100nF package="100 mil [THT, multilayer]"]
  C15 = Ceramic Capacitor [capacitance=100nF package="100 mil [THT, multilayer]"]
  U3 = Voltage Regulator - 5V [package="TO220 [THT]"]
  J7 = male pin header, 3 pins [form="♂ (male)"]
  J9 = male pin header, 3 pins [form="♂ (male)"]
  RFM12b1 = RFM12b HopeRF Transceiver
  J10 = female pin header, 1 pin [form="♀ (female)"]
  R3 = Resistor [tolerance=±5% resistance=4.7k package=THT]
  R2 = Resistor [tolerance=±5% resistance=10k package=THT]
  R6 = Resistor [tolerance=±5% resistance=4.7k package=THT]
  R4 = Resistor [tolerance=±5% resistance=10k package=THT]
  R7 = Resistor [tolerance=±5% resistance=4.7k package=THT]
  R5 = Resistor [tolerance=±5% resistance=10k package=THT]
  U2 = atmega328 [package=dip]
  Bauteil1 = EZ1117
  Arduino1 = Arduino

nets:
  N1: S2.Pin_1, S2.Pin_2, R1.Pin_1, C10.1, J7.pin1, U2.RESET
  GND: S2.Pin_3, S2.Pin_4, C8.0, C9.1, J6.pin1, Power.GND, C11.-, C12.1, C13.0, C15.0, U3.GND, J9.pin1, RFM12b1.10_GND, R2.Pin_1, R4.Pin_1, R5.Pin_1, U2.GND, Bauteil1.GND/ADJ, Arduino1.GND
  N2: XTAL1.pin_0, C8.1, U2.XLAT1
  N3: XTAL1.pin_1, C9.0, U2.XLAT2
  VCC: R1.Pin_0, J6.pin3, C13.1, C15.1, U3.output_voltage, J9.pin3, U2.VCC, U2.AVCC, Bauteil1.Vin, Arduino1.+5V
  N4: C10.0, J6.pin6
  N5: J6.pin4, U2.D0_(RX), Arduino1.D0RX
  N6: J6.pin5, U2.D1_(TX), Arduino1.D1TX
  N7: Power.VCC, D1.anode
  N8: D1.cathode, C11.+, C12.0, U3.input_voltage
  N9: J7.pin2, R6.Pin_0, U2.D13, Arduino1.D13
  N10: J7.pin3, RFM12b1.1_SDO, U2.D12, Arduino1.D12
  N11: J9.pin2, R3.Pin_0, U2.D11_(PWM), Arduino1.D11
  N12: RFM12b1.2_nIRQ, U2.D2, Arduino1.D2
  N13: RFM12b1.8_ANT, J10.pin1
  N14: RFM12b1.9_VDD, Bauteil1.Vout, Arduino1.3V3
  N15: RFM12b1.12_SDI, R3.Pin_1, R2.Pin_0
  N16: RFM12b1.13_SCK, R6.Pin_1, R4.Pin_0
  N17: RFM12b1.14_nSEL, R7.Pin_1, R5.Pin_0
  N18: R7.Pin_0, U2.D10_(PWM), Arduino1.D10
  N19: U2.D3_(PWM), Arduino1.D3
  N20: U2.D4, Arduino1.D4
  N21: U2.D5_(PWM), Arduino1.D5
  N22: U2.D6_(PWM), Arduino1.D6
  N23: U2.D7, Arduino1.D7
  N24: U2.D8, Arduino1.D8
  N25: U2.D9_(PWM), Arduino1.D9
  N26: U2.AREF, Arduino1.aref
  N27: U2.A0, Arduino1.A0
  N28: U2.A1, Arduino1.A1
  N29: U2.A2, Arduino1.A2
  N30: U2.A3, Arduino1.A3
  N31: U2.A4, Arduino1.A4
  N32: U2.A5, Arduino1.A5

notes:
  RFBoard
  V1.3
  arduino-praxis.ch/rfboard
  Ant
  FTDI
  0V
  +5V
  ICSP
  1
  2
  ATmega328
  A0
  A1
  A2
  A3
  A4
  A5
  Vin
  GND
  5V
  3.3V
